# Fritzing sketch bytebee85-production-planb (saved by Fritzing 0.9.9b)
circuit board: 4.5cm x 4cm
breadboards: 1

parts:
  U2 = attiny85 [package=dip]
  10K = Resistor [tolerance=±5% power=0.25 resistance=10k package=THT]
  LED2 = LED - 5mm [color="Red (633nm)" current=0.030 package="5 mm [THT]"]
  Button = Pushbutton [package="[THT]"]
  POT = Rotary Potentiometer (Large) [maximum_resistance=100kΩ package=THT]
  VCC2 = Battery
  TRS3 = Audio Jack (TRS) 3.5mm [package="4Ucon 08780 [THT]"]
  TRS4 = Audio Jack (TRS) 3.5mm [package="4Ucon 08780 [THT]"]
  10K_2 = Resistor [tolerance=±5% power=0.25 resistance=10k package=THT]
  10K_3 = Resistor [tolerance=±5% power=0.25 resistance=10k package=THT]
  1k = Resistor [tolerance=±5% power=0.25 resistance=1k package=THT]
  C104 = Ceramic Capacitor [capacitance=100nF voltage=35V package="200 mil [THT, multilayer]"]

nets:
  N1: U2.Pin_2, 10K.Pin_0, 10K_2.Pin_1, 10K_3.Pin_1, C104.1
  N2: U2.Pin_3, POT.wiper
  GND: U2.Pin_4, Button.Pin_3, Button.Pin_4, POT.leg2, VCC2.-, TRS3.Sleeve, TRS4.Sleeve, 10K_3.Pin_0, 1k.Pin_0
  N3: U2.Pin_6, LED2.anode, TRS3.Tip
  3V: U2.Pin_8, POT.leg1, VCC2.+, 10K_2.Pin_0
  N4: 10K.Pin_1, Button.Pin_1, Button.Pin_2
  N5: LED2.cathode, 1k.Pin_1
  N6: TRS4.Ring, C104.0

notes:
  PROGRAMMER IN (RING)
  Button Left ++
  Pot2
  Bootloader indicator
  AUDIO OUT (TIP)
  gnd
  PROG IN
  AUDIO OUT
  ATTINY85
  +3V/+5V
  -
  +
