# Fritzing sketch bytebee85-withoutprogrammer (saved by Fritzing 0.9.9b)

parts:
  U1 = attiny85 [package=dip]
  R1 = Resistor [tolerance=±5% power=0.25 resistance=1k package=THT]
  LED1 = LED - 5mm [color="Red (633nm)" current=0.030 package="5 mm [THT]"]
  S1 = Pushbutton [package="[THT]"]
  R4 = Rotary Potentiometer (Large) [maximum_resistance=100kΩ package=THT]
  VCC1 = Battery
  TRS2 = Audio Jack (TRS) 3.5mm [package="4Ucon 08780 [THT]"]
  R5 = Resistor [tolerance=±5% power=0.25 resistance=10k package=THT]

nets:
  N1: U1.Pin_2, R5.Pin_0
  N2: U1.Pin_3, R4.wiper
  N3: U1.Pin_4, R1.Pin_0, S1.Pin_4, R4.leg2, VCC1.-, TRS2.Sleeve
  N4: U1.Pin_6, LED1.anode, TRS2.Tip
  N5: U1.Pin_8, R4.leg1, VCC1.+
  N6: R1.Pin_1, LED1.cathode
  N7: S1.Pin_1, S1.Pin_2, R5.Pin_1

notes:
  AUDIO OUT (TIP)
  Bootloader indicator
  Pot2
  Button Left ++
  10k
  1k
